// Logisim project Lab_5.circ as structural Verilog: 5 circuits, main circuit main
module main (
  input  Cin,
  input  [7:0] B,
  input  [7:0] A,
  output [7:0] S,
  output Cout
);

  Ripple_Carry_Adder_8Bit ripple_carry_adder_8bit_1 (.Cin(Cin), .A(A), .B(B), .S(S), .Cout(Cout));
endmodule

module Ripple_Carry_Adder_4Bit (
  input  cin,
  input  [3:0] A,
  input  [3:0] B,
  output [3:0] S,
  output cout
);

  wire adder_1_cout, adder_2_cout, adder_3_cout;

  Adder #(.width(1)) adder_1 (.a(A[0]), .b(B[0]), .out(S[0]), .cin(cin), .cout(adder_1_cout));
  Adder #(.width(1)) adder_2 (.a(A[1]), .b(B[1]), .out(S[1]), .cin(adder_1_cout), .cout(adder_2_cout));
  Adder #(.width(1)) adder_3 (.a(A[2]), .b(B[2]), .out(S[2]), .cin(adder_2_cout), .cout(adder_3_cout));
  Adder #(.width(1)) adder_4 (.a(A[3]), .b(B[3]), .out(S[3]), .cin(adder_3_cout), .cout(cout));
endmodule

module Accumulator_8Bit (
  input  Cin,
  input  [7:0] A,
  input  clk,
  output [7:0] S,
  output Overflow
);

  wire d_ff_1_qn, ripple_carry_adder_8bit_1_cout;
  wire [7:0] ripple_carry_adder_8bit_1_s, shift_register_1_out;

  Shift_Register #(.length(1), .parallel("false"), .width(8)) shift_register_1 (
    .shift(1'b1), .in(A), .clk(clk), .out(shift_register_1_out), .clr(1'b0));  // open: load, d0, q0
  Ripple_Carry_Adder_8Bit ripple_carry_adder_8bit_1 (
    .Cin(Cin), .A(S), .B(shift_register_1_out), .S(ripple_carry_adder_8bit_1_s),
    .Cout(ripple_carry_adder_8bit_1_cout));
  Shift_Register #(.length(1), .parallel("false"), .width(8)) shift_register_2 (
    .shift(1'b1), .in(ripple_carry_adder_8bit_1_s), .clk(clk), .out(S), .clr(1'b0));  // open: load, d0, q0
  D_Flip_Flop d_ff_1 (
    .D(ripple_carry_adder_8bit_1_cout), .clk(clk), .Q(Overflow), .Qn(d_ff_1_qn), .preset(1'b0), .reset(1'b0));
  // NoConnect on d_ff_1_qn
endmodule

module Ripple_Carry_Adder_8Bit (
  input  Cin,
  input  [7:0] A,
  input  [7:0] B,
  output [7:0] S,
  output Cout
);

  wire ripple_carry_adder_4bit_1_cout;

  Ripple_Carry_Adder_4Bit ripple_carry_adder_4bit_1 (
    .cin(Cin), .A(A[3:0]), .B(B[3:0]), .S(S[3:0]), .cout(ripple_carry_adder_4bit_1_cout));
  Ripple_Carry_Adder_4Bit ripple_carry_adder_4bit_2 (
    .cin(ripple_carry_adder_4bit_1_cout), .A(A[7:4]), .B(B[7:4]), .S(S[7:4]), .cout(Cout));
endmodule

module Add_Sub_Accumulator (
  input  in_1,
  input  [7:0] in_2,
  output [7:0] out_3,
  output overflow,
  output overflow_2s
);

  wire [7:0] multiplexer_1_out, not_1_out, ripple_carry_adder_8bit_1_s;

  assign not_1_out = ~in_2;  // NOT_Gate not_1, 8 bits wide
  Ripple_Carry_Adder_8Bit ripple_carry_adder_8bit_1 (
    .Cin(1'b0), .A(not_1_out), .B(8'h1), .S(ripple_carry_adder_8bit_1_s), .Cout(overflow_2s));
  Multiplexer #(.width(8)) multiplexer_1 (
    .in0(in_2), .in1(ripple_carry_adder_8bit_1_s), .out(multiplexer_1_out), .sel(in_1));
  // Accumulator_8Bit accumulator_8bit_1: pin names not known; wires that end beside it: multiplexer_1_out, out_3, overflow
endmodule
